// Logisim project guess-the-number-x.circ as structural Verilog
module decoder (
  input  A,
  input  B,
  input  C,
  input  D,
  output up1,
  output up2,
  output up3,
  output up4,
  output down1,
  output down2,
  output down3,
  output down4
);

  wire and_1_out, and_2_out, and_3_out, and_4_out, and_5_out, and_6_out, and_7_out, and_8_out, and_9_out,
       and_10_out, and_11_out, and_12_out, and_13_out, and_14_out, and_15_out, and_16_out, and_17_out,
       and_18_out, and_19_out, and_20_out, and_21_out, and_22_out, and_23_out, and_24_out, and_25_out,
       and_26_out, and_27_out, and_28_out, and_29_out, and_30_out, and_31_out, and_32_out, and_33_out,
       and_34_out, and_35_out, not_1_out, not_2_out, not_3_out, not_4_out;

  not not_1 (not_1_out, A);
  not not_2 (not_2_out, B);
  not not_3 (not_3_out, C);
  not not_4 (not_4_out, D);
  and and_1 (and_1_out, not_2_out, not_4_out);
  and and_2 (and_2_out, not_1_out, C);
  and and_3 (and_3_out, not_1_out, B, D);
  and and_4 (and_4_out, A, not_2_out, not_3_out);
  and and_5 (and_5_out, A, not_4_out);
  and and_6 (and_6_out, B, C);
  and and_7 (and_7_out, not_1_out, not_3_out, not_4_out);
  and and_8 (and_8_out, not_1_out, C, D);
  and and_9 (and_9_out, not_2_out, not_4_out);
  and and_10 (and_10_out, A, not_3_out, D);
  and and_11 (and_11_out, not_1_out, not_2_out);
  and and_12 (and_12_out, not_1_out, B);
  and and_13 (and_13_out, A, not_2_out);
  and and_14 (and_14_out, not_3_out, D);
  and and_15 (and_15_out, not_2_out, not_3_out);
  and and_16 (and_16_out, not_2_out, D);
  and and_17 (and_17_out, B, not_3_out, D);
  and and_18 (and_18_out, not_1_out, not_2_out, not_4_out);
  and and_19 (and_19_out, not_2_out, C, D);
  and and_20 (and_20_out, A, not_3_out);
  and and_21 (and_21_out, B, C, not_4_out);
  and and_22 (and_22_out, not_2_out, not_4_out);
  and and_23 (and_23_out, C, not_4_out);
  and and_24 (and_24_out, A, C);
  and and_25 (and_25_out, A, B);
  and and_26 (and_26_out, not_3_out, not_4_out);
  and and_27 (and_27_out, not_1_out, B, not_3_out);
  and and_28 (and_28_out, B, not_4_out);
  and and_29 (and_29_out, A, not_2_out);
  and and_30 (and_30_out, A, C);
  and and_31 (and_31_out, not_2_out, C);
  and and_32 (and_32_out, A, not_2_out);
  and and_33 (and_33_out, not_1_out, B, not_3_out);
  and and_34 (and_34_out, C, not_4_out);
  and and_35 (and_35_out, A, D);
  or or_1 (up3, and_1_out, and_2_out, and_3_out, and_4_out, and_5_out, and_6_out);
  or or_2 (up4, and_7_out, and_8_out, and_9_out, and_10_out, and_11_out);
  or or_3 (down3, and_12_out, and_13_out, and_14_out, and_15_out, and_16_out);
  or or_4 (down2, and_17_out, and_18_out, and_19_out, and_20_out, and_21_out);
  or or_5 (down1, and_22_out, and_23_out, and_24_out, and_25_out);
  or or_6 (up2, and_26_out, and_27_out, and_28_out, and_29_out, and_30_out);
  or or_7 (up1, and_31_out, and_32_out, and_33_out, and_34_out, and_35_out);

  assign down4 = 1'b0;

  // Notes on the sheet:
  //   UP 1
  //   UP 2
  //   UP 3
  //   UP 4
  //   DOWN 1
  //   DOWN 2
  //   DOWN 3
  //   DOWN 4
endmodule

module cronometro (
  input  clk,
  input  x_jogando,
  input  cfg,
  input  s0,
  input  s1,
  input  m0,
  input  m1,
  input  reset,
  output fim,
  output [3:0] s0_2,
  output [3:0] s1_2,
  output [3:0] m0_2,
  output [3:0] m1_2
);

  wire and_1_out, borrows0, borrows1, borrows2, comparator_1_eq, comparator_2_eq, comparator_3_eq,
       comparator_4_eq, decoder_1_down1, decoder_1_down2, decoder_1_down3, decoder_1_down4, decoder_1_up1,
       decoder_1_up2, decoder_1_up3, decoder_1_up4, decoder_2_down1, decoder_2_down2, decoder_2_down3,
       decoder_2_down4, decoder_2_up1, decoder_2_up2, decoder_2_up3, decoder_2_up4, decoder_3_down1,
       decoder_3_down2, decoder_3_down3, decoder_3_down4, decoder_3_up1, decoder_3_up2, decoder_3_up3,
       decoder_3_up4, decoder_4_down1, decoder_4_down2, decoder_4_down3, decoder_4_down4, decoder_4_up1,
       decoder_4_up2, decoder_4_up3, decoder_4_up4, multiplexer_1_out, multiplexer_2_out, multiplexer_3_out,
       multiplexer_4_out, not_1_out, not_2_out;

  not not_1 (not_1_out, fim);
  not not_2 (not_2_out, cfg);
  and and_1 (and_1_out, not_1_out, clk, x_jogando, not_2_out);
  Multiplexer #(.enable("false")) multiplexer_1 (.in0(and_1_out), .in1(s0), .out(multiplexer_1_out), .sel(cfg));
  Multiplexer #(.enable("false")) multiplexer_2 (.in0(borrows0), .in1(s1), .out(multiplexer_2_out), .sel(cfg));
  Multiplexer #(.enable("false")) multiplexer_3 (.in0(borrows1), .in1(m0), .out(multiplexer_3_out), .sel(cfg));
  Multiplexer #(.enable("false")) multiplexer_4 (.in0(borrows2), .in1(m1), .out(multiplexer_4_out), .sel(cfg));
  Comparator #(.width(4)) comparator_1 (.a(4'b0000), .b(s0_2), .eq(comparator_1_eq));  // open: gt, lt
  Comparator #(.width(4)) comparator_2 (.a(4'b0000), .b(s1_2), .eq(comparator_2_eq));  // open: gt, lt
  Comparator #(.width(4)) comparator_3 (.a(4'b0000), .b(m0_2), .eq(comparator_3_eq));  // open: gt, lt
  Comparator #(.width(4)) comparator_4 (.a(4'b0000), .b(m1_2), .eq(comparator_4_eq));  // open: gt, lt
  Counter #(.width(4), .max('h9)) u_s0 (
    .Q(s0_2), .carry(borrows0), .clk(multiplexer_1_out), .clr(reset), .down(1'b1));  // open: load, D, count, preset
  Counter #(.width(4), .max('h5), .trigger("falling")) u_s1 (
    .Q(s1_2), .carry(borrows1), .clk(multiplexer_2_out), .clr(reset), .down(1'b1));  // open: load, D, count, preset
  Counter #(.width(4), .max('h9), .trigger("falling")) u_m0 (
    .Q(m0_2), .carry(borrows2), .clk(multiplexer_3_out), .clr(reset), .down(1'b1));  // open: load, D, count, preset
  Counter #(.width(4), .max('h5), .trigger("falling")) u_m1 (
    .Q(m1_2), .clk(multiplexer_4_out), .clr(reset), .down(1'b1));  // open: load, D, count, carry, preset
  and and_2 (fim, comparator_1_eq, comparator_2_eq, comparator_3_eq, comparator_4_eq);
  decoder decoder_1 (
    .A(s0_2[3]), .B(s0_2[2]), .C(s0_2[1]), .D(s0_2[0]), .up1(decoder_1_up1), .up2(decoder_1_up2),
    .up3(decoder_1_up3), .up4(decoder_1_up4), .down1(decoder_1_down1), .down2(decoder_1_down2),
    .down3(decoder_1_down3), .down4(decoder_1_down4));
  decoder decoder_2 (
    .A(s1_2[3]), .B(s1_2[2]), .C(s1_2[1]), .D(s1_2[0]), .up1(decoder_2_up1), .up2(decoder_2_up2),
    .up3(decoder_2_up3), .up4(decoder_2_up4), .down1(decoder_2_down1), .down2(decoder_2_down2),
    .down3(decoder_2_down3), .down4(decoder_2_down4));
  decoder decoder_3 (
    .A(m0_2[3]), .B(m0_2[2]), .C(m0_2[1]), .D(m0_2[0]), .up1(decoder_3_up1), .up2(decoder_3_up2),
    .up3(decoder_3_up3), .up4(decoder_3_up4), .down1(decoder_3_down1), .down2(decoder_3_down2),
    .down3(decoder_3_down3), .down4(decoder_3_down4));
  decoder decoder_4 (
    .A(m1_2[3]), .B(m1_2[2]), .C(m1_2[1]), .D(m1_2[0]), .up1(decoder_4_up1), .up2(decoder_4_up2),
    .up3(decoder_4_up3), .up4(decoder_4_up4), .down1(decoder_4_down1), .down2(decoder_4_down2),
    .down3(decoder_4_down3), .down4(decoder_4_down4));
  _7_Segment_Display u_7_segment_display_1 (
    .g(decoder_4_up1), .f(decoder_4_up2), .a(decoder_4_up3), .b(decoder_4_up4), .e(decoder_4_down1),
    .d(decoder_4_down2), .c(decoder_4_down3), .dp(decoder_4_down4));
  _7_Segment_Display u_7_segment_display_2 (
    .g(decoder_3_up1), .f(decoder_3_up2), .a(decoder_3_up3), .b(decoder_3_up4), .e(decoder_3_down1),
    .d(decoder_3_down2), .c(decoder_3_down3), .dp(decoder_3_down4));
  _7_Segment_Display u_7_segment_display_3 (
    .g(decoder_2_up1), .f(decoder_2_up2), .a(decoder_2_up3), .b(decoder_2_up4), .e(decoder_2_down1),
    .d(decoder_2_down2), .c(decoder_2_down3), .dp(decoder_2_down4));
  _7_Segment_Display u_7_segment_display_4 (
    .g(decoder_1_up1), .f(decoder_1_up2), .a(decoder_1_up3), .b(decoder_1_up4), .e(decoder_1_down1),
    .d(decoder_1_down2), .c(decoder_1_down3), .dp(decoder_1_down4));

  // Other names for the same wires on the sheet: modo = cfg; saidam0[3:0] = m0_2; saidam1[3:0] = m1_2;
  //   saidas0[3:0] = s0_2; saidas1[3:0] = s1_2

  // Notes on the sheet:
  //   clock
  //   0 jogo$1 config
  //   CONDICOES JOGO
  //   +CLOCK
  //   MUDAR NO MODO $CONFIG
  //   FIM
  //   SAIDAS
  //   AQUI É TEMPORÁRIO SÓ PRA PODER
  //   MM : SS
  //   :
  //   VISUALIZAR NO CIRCUITO
endmodule
